# Fritzing sketch guerra_galaxias (saved by Fritzing 0.9.3b)
breadboards: 1

parts:
  Componente1 = Arduino Nano (Rev3.0)
  J1 = Piezo Speaker

nets:
  N1: Componente1.GND, J1.pin1
  N2: Componente1.D11/MOSI, J1.pin2
